// Logisim project Task 4 - Circuit 1.circ as structural Verilog: 1 circuit, main circuit main
module main (
  input  A,
  input  B,
  input  C,
  output out_4
);

  wire _1_out, _2_out, _3_out, _4_out, not_1_out;

  not not_1 (not_1_out, C);
  and _1 (_1_out, A, B);
  and _2 (_2_out, A, C);
  or _3 (_3_out, B, not_1_out);
  nand _4 (_4_out, _1_out, _2_out);
  xnor _5 (out_4, _4_out, _3_out);
endmodule
