// Logisim project Task 4 - Circuit 2.circ as structural Verilog: 1 circuit, main circuit main
module main (
  input  A,
  input  B,
  input  C,
  output out_4
);

  wire _6_out, not_1_out, not_2_out;

  not not_1 (not_1_out, A);
  not not_2 (not_2_out, C);
  and _6 (_6_out, not_1_out, B);
  or _7 (out_4, _6_out, not_2_out);
endmodule
